# Fritzing sketch led (saved by Fritzing 0.9.2b)
breadboards: 1

parts:
  Parte1 = Arduino Leonardo (Rev3b)
  R1 = Resistor [tolerance=±5% resistance=330 package="2010 [SMD]"]
  R2 = Resistor [tolerance=±5% resistance=330 package="2010 [SMD]"]
  R3 = Resistor [tolerance=±5% resistance=330 package="2010 [SMD]"]
  R4 = Resistor [tolerance=±5% resistance=330 package="2010 [SMD]"]
  LED5 = smd LED [color="Red (633nm)" package="0603 [SMD]"]
  LED6 = smd LED [color="Orange (612nm)" package="0603 [SMD]"]
  LED7 = smd LED [color="Green (570nm)" package="0603 [SMD]"]
  LED8 = smd LED [color="White (6500K)" package="0603 [SMD]"]

nets:
  N1: Parte1.GND, LED5.cathode, LED6.cathode, LED7.cathode, LED8.cathode
  N2: Parte1.D9_PWM/A9, R4.Pin_0
  N3: Parte1.D10_PWM/A10, R3.Pin_0
  N4: Parte1.D11_PWM, R2.Pin_0
  N5: Parte1.D12/A11, R1.Pin_0
  N6: R1.Pin_1, LED5.anode
  N7: R2.Pin_1, LED6.anode
  N8: R3.Pin_1, LED7.anode
  N9: R4.Pin_1, LED8.anode
